# Fritzing sketch Capstone Fritzing (saved by Fritzing 0.9.4)
breadboards: 1

parts:
  Argon1 = Particle Argon
  OLED_I2C1 = OLED 128x64 I2C Monochrome Display
  J1 = Basic Servo
  Water_Level_Sensor1 = Water Level Sensor
  Water_Level_Sensor2 = Water Level Sensor
  Part1 = MQ-3 breakout
  Relay1 = Relay - 6 pins [package="DIP (Dual Inline) [THT]"]
  Part2 = HC-SR501 Body Sensor Module

nets:
  VCC: Argon1.3.3V, Water_Level_Sensor1.VCC, Water_Level_Sensor2.VCC, Relay1.VCC
  GND: Argon1.GND, OLED_I2C1.GND, Water_Level_Sensor1.GND, Water_Level_Sensor2.GND, Relay1.GND
  N1: Argon1.A0, Water_Level_Sensor1.SIG
  N2: Argon1.A1, Water_Level_Sensor2.SIG
  N3: Argon1.A2, Part2.OUT
  N4: Argon1.A3, Part1.AO
  N5: Argon1.SDA, OLED_I2C1.SDA
  N6: Argon1.SCL, OLED_I2C1.SCK
  N7: Argon1.D5, J1.pulse
  N8: Argon1.D6, Relay1.IN
  VCC_2: OLED_I2C1.VDD, J1.vcc, Part1.VCC, Part2.VCC
  GND_2: J1.gnd, Part1.GND, Part2.GND

custom parts:
  Particle Argon: The Argon is a powerful Wi-Fi enabled development board that can act as either a standalone Wi-Fi endpoint or Wi-Fi enabled gateway for Particle Mesh networks. It is based on the Nordic nRF52840 and has built-in battery charging circuitry so it’s easy to connect a Li-Po and deploy your local network in minutes. The Argon is great for connecting existing projects to the Particle Device Cloud or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
  Water Level Sensor: A water level sensor. This sensor operates at 3V to 5V. The Sig (signal) pin outputs an analogue signal that is in proportion to the amount of water in contact with the sensor.
  MQ-3 breakout: Alcohol sensor is capable of detecting alcohol (ethanol) particles on itself and gives the information in digital form back to us to manipulate with it. SKU:101251 • Voltage: 5V DC • Power: max 750mW • Measurement range: 0.04-4mg/L
  Relay - 6 pins: A DIP stand-in part for whatever IC you want. With 6 pins on a 900mil dual inline package (DIP) footprint.
  HC-SR501 Body Sensor Module: Pyroelectric Infrared PIR Motion Sensor Detector Module
